// Logisim project 74138.circ as structural Verilog: 1 circuit, main circuit main
module main (
  output out_1,
  output out_2,
  output out_3,
  output out_4,
  output out_5,
  output out_6,
  output out_7,
  output out_8
);

  wire and_1_out, not_1_out, not_2_out, not_3_out, not_4_out, not_5_out, not_6_out;

  not not_1 (not_1_out, 1'b1);
  not not_2 (not_2_out, not_1_out);
  nand nand_1 (out_1, not_2_out, not_5_out, not_6_out, and_1_out);
  not not_3 (not_3_out, 1'b0);
  not not_4 (not_4_out, 1'b1);
  not not_5 (not_5_out, not_4_out);
  not not_6 (not_6_out, not_3_out);
  nand nand_2 (out_2, and_1_out, not_6_out, not_2_out, not_4_out);
  nand nand_3 (out_3, and_1_out, not_5_out, not_2_out, not_3_out);
  nand nand_4 (out_4, and_1_out, not_2_out, not_3_out, not_4_out);
  nand nand_5 (out_5, and_1_out, not_1_out, not_6_out, not_5_out);
  and and_1 (and_1_out, ~1'b0, ~1'b0, 1'b1);  // AND_Gate
  nand nand_6 (out_6, and_1_out, not_1_out, not_6_out, not_4_out);
  nand nand_7 (out_7, and_1_out, not_1_out, not_3_out, not_5_out);
  nand nand_8 (out_8, and_1_out, not_1_out, not_3_out, not_4_out);
endmodule
